# Fritzing sketch ESP-GNSS-Tracker (saved by Fritzing 0.9.10b)
breadboards: 1

parts:
  MH-ET_Live_Minikit_for_ESP1 = MH-ET Live Minikit for ESP32
  S1 = Pushbutton [package="[THT]"]
  o1 = Module display OLED I2C 128x64 SSD1306 [package=THT]
  sdCard1 = my_sdCard
  R1 = Resistor [tolerance=±5% resistance=220 package="0603 [SMD]"]

nets:
  N1: MH-ET_Live_Minikit_for_ESP1.IO18, sdCard1.SCK
  N2: MH-ET_Live_Minikit_for_ESP1.IO19, sdCard1.MISO
  GND: MH-ET_Live_Minikit_for_ESP1.IO23, o1.GND, sdCard1.GND, sdCard1.MOSI, R1.Pin_1
  VCC: MH-ET_Live_Minikit_for_ESP1.IO5, S1.Pin_3, S1.Pin_4, o1.VCC, sdCard1.VCC, sdCard1.CS
  N3: MH-ET_Live_Minikit_for_ESP1.IO22, o1.SCL
  N4: MH-ET_Live_Minikit_for_ESP1.IO21, o1.SDA
  N5: MH-ET_Live_Minikit_for_ESP1.IO4, S1.Pin_1, S1.Pin_2, R1.Pin_0

notes:
  GNSS Modul via
  Rx / Tx

custom parts:
  MH-ET Live Minikit for ESP32: MH-ET Live Minikit for ESP32 ( http://mh.nodebb.com/topic/8/mh-et-live-minikit-for-esp32/2/) PCB footprint is invalid.
  Module display OLED I2C 128x64 SSD1306: Ecran OLED I2C SSD163 de 128x64 avec connexion I2C
  my_sdCard: micro sdCard Adapter with 90º pin header. Use a filtering Capacitor between CS and GND if needed. PCB View Pinouts are Reversed for laying parallel on PCB using a 90º pin header.
